# Fritzing sketch ardusub_altimeter_aj-sr04m (saved by Fritzing 0.9.3b)
breadboards: 1

parts:
  R1 = Resistor [tolerance=±5% resistance=1k package="2010 [SMD]"]
  R2 = Resistor [tolerance=±5% resistance=2k package="2010 [SMD]"]
  Raspberry_Pi_1 = Raspberry Pi 3 [part_number=RPI-3-V1.2]
  hc-sr1 = hc-sr04

nets:
  N1: R1.Pin_0, hc-sr1.Echo
  N2: R1.Pin_1, R2.Pin_0, Raspberry_Pi_1.GIPO24
  GND: R2.Pin_1, Raspberry_Pi_1.GND, hc-sr1.GND
  N3: Raspberry_Pi_1.GIPO23, hc-sr1.Trig
  5V: Raspberry_Pi_1.5V, hc-sr1.VCC
